// Logisim project CPU2.circ as structural Verilog: 18 circuits, main circuit main
module main (
);

  wire processor_1_rom_enable;
  wire [15:0] processor_1_rom_address, rom_1_data;

  ROM #(.addrWidth(16), .dataWidth(16)) rom_1 (
    .addr(processor_1_rom_address), .data(rom_1_data), .sel(processor_1_rom_enable));
  Processor processor_1 (
    .ROM_in(rom_1_data), .ROM_address(processor_1_rom_address), .ROM_enable(processor_1_rom_enable));  // open: RAM_in, RAM_address, RAM_value, RAM_SET, RAM_GET, Keyboard_Value_In, Keyboard_Set, Screen_Address, Screen_Value, Screen_Set

  // Notes on the sheet:
  //   contents of rom_1 (hex, n*v repeats v):
  //   1 2 3 4 5 6 7 8 9 a b c d e f
endmodule

module adder (
  input  b,
  input  a,
  input  C_in,
  output A_out,
  output C_out
);

  wire and_1_out, and_2_out, buffer_1_out, or_1_out, xor_1_out, xor_2_out;

  buf buffer_1 (buffer_1_out, C_in);
  and and_1 (and_1_out, a, b);
  xor xor_1 (xor_1_out, b, a);
  xor xor_2 (xor_2_out, xor_1_out, buffer_1_out);
  or or_1 (or_1_out, and_1_out, and_2_out);
  and and_2 (and_2_out, xor_1_out, buffer_1_out);
  buf buffer_2 (C_out, or_1_out);
  buf buffer_3 (A_out, xor_2_out);

  // Notes on the sheet:
  //   Result
endmodule

module _16_adder (
  input  [15:0] B,
  input  [15:0] A,
  output [15:0] out
);

  wire adder_1_c_out, adder_2_c_out, adder_3_c_out, adder_4_c_out, adder_5_c_out, adder_6_c_out,
       adder_7_c_out, adder_8_c_out, adder_9_c_out, adder_10_c_out, adder_11_c_out, adder_12_c_out,
       adder_13_c_out, adder_14_c_out, adder_15_c_out, adder_16_c_out;

  adder adder_1 (.b(B[15]), .a(A[15]), .C_in(adder_2_c_out), .A_out(out[15]), .C_out(adder_1_c_out));
  adder adder_2 (.b(B[14]), .a(A[14]), .C_in(adder_3_c_out), .A_out(out[14]), .C_out(adder_2_c_out));
  adder adder_3 (.b(B[13]), .a(A[13]), .C_in(adder_4_c_out), .A_out(out[13]), .C_out(adder_3_c_out));
  adder adder_4 (.b(B[12]), .a(A[12]), .C_in(adder_5_c_out), .A_out(out[12]), .C_out(adder_4_c_out));
  adder adder_5 (.b(B[11]), .a(A[11]), .C_in(adder_6_c_out), .A_out(out[11]), .C_out(adder_5_c_out));
  adder adder_6 (.b(B[10]), .a(A[10]), .C_in(adder_7_c_out), .A_out(out[10]), .C_out(adder_6_c_out));
  adder adder_7 (.b(B[9]), .a(A[9]), .C_in(adder_8_c_out), .A_out(out[9]), .C_out(adder_7_c_out));
  adder adder_8 (.b(B[8]), .a(A[8]), .C_in(adder_9_c_out), .A_out(out[8]), .C_out(adder_8_c_out));
  adder adder_9 (.b(B[7]), .a(A[7]), .C_in(adder_10_c_out), .A_out(out[7]), .C_out(adder_9_c_out));
  adder adder_10 (.b(B[6]), .a(A[6]), .C_in(adder_11_c_out), .A_out(out[6]), .C_out(adder_10_c_out));
  adder adder_11 (.b(B[5]), .a(A[5]), .C_in(adder_12_c_out), .A_out(out[5]), .C_out(adder_11_c_out));
  adder adder_12 (.b(B[4]), .a(A[4]), .C_in(adder_13_c_out), .A_out(out[4]), .C_out(adder_12_c_out));
  adder adder_13 (.b(B[3]), .a(A[3]), .C_in(adder_14_c_out), .A_out(out[3]), .C_out(adder_13_c_out));
  adder adder_14 (.b(B[2]), .a(A[2]), .C_in(adder_15_c_out), .A_out(out[2]), .C_out(adder_14_c_out));
  adder adder_15 (.b(B[1]), .a(A[1]), .C_in(adder_16_c_out), .A_out(out[1]), .C_out(adder_15_c_out));
  adder adder_16 (.b(B[0]), .a(A[0]), .C_in(1'b0), .A_out(out[0]), .C_out(adder_16_c_out));
endmodule

module _16_twos_compliment (
  input  [15:0] in_1,
  output [15:0] out_2
);

  wire [15:0] not_1_out;

  assign not_1_out = ~in_1;  // NOT_Gate not_1, 16 bits wide
  _16_adder u_16_adder_1 (.B(16'h1), .A(not_1_out), .out(out_2));
endmodule

module Processor (
  input  [15:0] RAM_in,
  input  [15:0] ROM_in,
  input  [7:0] Keyboard_Value_In,
  input  Keyboard_Set,
  output RAM_SET,
  output RAM_GET,
  output [15:0] RAM_address,
  output [15:0] RAM_value,
  output [9:0] Screen_Address,
  output [15:0] Screen_Value,
  output Screen_Set,
  output [15:0] ROM_address,
  output ROM_enable
);

  wire clock_1_out, demultiplexer_1_out0, demultiplexer_1_out1, demultiplexer_1_out2, not_1_out, or_1_out;
  wire [1:0] counter_1_q;
  wire [15:0] buffer_1_out, counter_2_q, register_1_q, register_2_q;

  Demultiplexer #(.select(2), .enable("false")) demultiplexer_1 (
    .out0(demultiplexer_1_out0), .out1(demultiplexer_1_out1), .out2(demultiplexer_1_out2), .in(1'b1),
    .sel(counter_1_q));  // open: out3
  Counter #(.width(2), .max('h2)) counter_1 (.Q(counter_1_q), .clk(clock_1_out));  // open: load, D, count, carry, clr
  not not_1 (not_1_out, clock_1_out);
  Clock clock_1 (.out(clock_1_out));
  assign buffer_1_out = ROM_in;  // Buffer buffer_1, 16 bits wide
  assign ROM_address = counter_2_q;  // Buffer buffer_2, 16 bits wide
  // Buffer buffer_3 has open pins: in=open, out=ROM_enable
  // Buffer buffer_4 has open pins: in=RAM_in, out=open
  Counter #(.width(16), .max('hffff)) counter_2 (
    .count(or_1_out), .Q(counter_2_q), .clk(not_1_out));  // open: load, D, carry, clr
  or or_1 (or_1_out, demultiplexer_1_out0, demultiplexer_1_out1);
  Register #(.width(16)) register_1 (
    .D(buffer_1_out), .en(demultiplexer_1_out1), .Q(register_1_q), .clk(not_1_out));  // open: clr
  Register #(.width(16)) register_2 (
    .D(buffer_1_out), .en(demultiplexer_1_out0), .Q(register_2_q), .clk(not_1_out));  // open: clr
  // Buffer buffer_5 has open pins: in=open, out=RAM_address
  // Buffer buffer_6 has open pins: in=Keyboard_Value_In, out=open
  // Buffer buffer_7 has open pins: in=open, out=RAM_value
  // Buffer buffer_8 has open pins: in=open, out=RAM_SET
  // Buffer buffer_9 has open pins: in=Keyboard_Set, out=open
  // Buffer buffer_10 has open pins: in=open, out=RAM_GET
  // Buffer buffer_11 has open pins: in=open, out=Screen_Address
  // Buffer buffer_12 has open pins: in=open, out=Screen_Value
  // Buffer buffer_13 has open pins: in=open, out=Screen_Set
endmodule

module ALU (
  input  ADD,
  input  SUB,
  input  MUL,
  input  [15:0] B,
  input  [15:0] A,
  output [15:0] OUT
);

  wire [15:0] adder_1_out, multiplier_1_out, subtractor_1_out;

  Adder #(.width(16)) adder_1 (.a(B), .b(A), .out(adder_1_out));  // open: cin, cout
  Subtractor #(.width(16)) subtractor_1 (.a(B), .b(A), .out(subtractor_1_out));  // open: bin, bout
  Multiplier #(.width(16)) multiplier_1 (.a(B), .b(A), .out(multiplier_1_out));  // open: cin, cout
  assign OUT = ADD ? adder_1_out : 16'bz;  // Controlled_Buffer controlled_buffer_1
  assign OUT = SUB ? subtractor_1_out : 16'bz;  // Controlled_Buffer controlled_buffer_2
  assign OUT = MUL ? multiplier_1_out : 16'bz;  // Controlled_Buffer controlled_buffer_3
endmodule

module _16_Shift_Left (
  input  [15:0] in,
  output [15:0] out
);


  assign out = {in[14:0], 1'b0};
endmodule

module _16_Shift_Right (
  input  [15:0] in,
  output [15:0] out
);


  assign out = {1'b0, in[15:1]};
endmodule

module _1_to_16_duplicator (
  input  in,
  output [15:0] out
);


  assign out = {16{in}};
endmodule

module _16_Least_Significant (
  input  [15:0] in_1,
  output out_2
);


  assign out_2 = in_1[0];
endmodule

module _16_multiply (
  input  [15:0] in_1,
  input  [15:0] in_2,
  output [15:0] out_3
);

  wire [15:0] multiplexer_1_out, multiplexer_2_out, multiplexer_3_out, multiplexer_4_out, multiplexer_5_out,
       multiplexer_6_out, multiplexer_7_out, multiplexer_8_out, multiplexer_9_out, multiplexer_10_out,
       multiplexer_11_out, multiplexer_12_out, multiplexer_13_out, multiplexer_14_out, multiplexer_15_out,
       multiplexer_16_out, n16_adder_1_out, n16_adder_2_out, n16_adder_3_out, n16_adder_4_out,
       n16_adder_5_out, n16_adder_6_out, n16_adder_7_out, n16_adder_9_out, n16_adder_10_out,
       n16_adder_11_out, n16_adder_12_out, n16_adder_13_out, n16_adder_14_out, n16_adder_15_out,
       n16_shift_left_1_out, n16_shift_left_2_out, n16_shift_left_3_out, n16_shift_left_4_out,
       n16_shift_left_5_out, n16_shift_left_6_out, n16_shift_left_7_out, n16_shift_left_8_out,
       n16_shift_left_9_out, n16_shift_left_10_out, n16_shift_left_11_out, n16_shift_left_12_out,
       n16_shift_left_13_out, n16_shift_left_14_out, n16_shift_left_15_out;

  _16_adder u_16_adder_1 (.B(multiplexer_1_out), .A(multiplexer_2_out), .out(n16_adder_1_out));
  Multiplexer #(.width(16), .enable("false")) multiplexer_1 (
    .in0({16{1'b0}}), .in1(in_1), .out(multiplexer_1_out), .sel(in_2[0]));
  _16_Shift_Left u_16_shift_left_1 (.in(in_1), .out(n16_shift_left_1_out));
  _16_adder u_16_adder_2 (.B(n16_adder_1_out), .A(n16_adder_4_out), .out(n16_adder_2_out));
  Multiplexer #(.width(16), .enable("false")) multiplexer_2 (
    .in0({16{1'b0}}), .in1(n16_shift_left_1_out), .out(multiplexer_2_out), .sel(in_2[1]));
  _16_Shift_Left u_16_shift_left_2 (.in(n16_shift_left_1_out), .out(n16_shift_left_2_out));
  _16_adder u_16_adder_3 (.B(n16_adder_2_out), .A(n16_adder_6_out), .out(n16_adder_3_out));
  _16_adder u_16_adder_4 (.B(multiplexer_4_out), .A(multiplexer_3_out), .out(n16_adder_4_out));
  Multiplexer #(.width(16), .enable("false")) multiplexer_3 (
    .in0({16{1'b0}}), .in1(n16_shift_left_4_out), .out(multiplexer_3_out), .sel(in_2[3]));
  Multiplexer #(.width(16), .enable("false")) multiplexer_4 (
    .in0({16{1'b0}}), .in1(n16_shift_left_2_out), .out(multiplexer_4_out), .sel(in_2[2]));
  _16_Shift_Left u_16_shift_left_3 (.in(n16_shift_left_4_out), .out(n16_shift_left_3_out));
  _16_Shift_Left u_16_shift_left_4 (.in(n16_shift_left_2_out), .out(n16_shift_left_4_out));
  _16_adder u_16_adder_5 (.B(multiplexer_5_out), .A(multiplexer_6_out), .out(n16_adder_5_out));
  Multiplexer #(.width(16), .enable("false")) multiplexer_5 (
    .in0({16{1'b0}}), .in1(n16_shift_left_3_out), .out(multiplexer_5_out), .sel(in_2[4]));
  _16_Shift_Left u_16_shift_left_5 (.in(n16_shift_left_3_out), .out(n16_shift_left_5_out));
  _16_adder u_16_adder_6 (.B(n16_adder_5_out), .A(n16_adder_7_out), .out(n16_adder_6_out));
  _16_adder u_16_adder_7 (.B(multiplexer_7_out), .A(multiplexer_8_out), .out(n16_adder_7_out));
  Multiplexer #(.width(16), .enable("false")) multiplexer_6 (
    .in0({16{1'b0}}), .in1(n16_shift_left_5_out), .out(multiplexer_6_out), .sel(in_2[5]));
  Multiplexer #(.width(16), .enable("false")) multiplexer_7 (
    .in0({16{1'b0}}), .in1(n16_shift_left_6_out), .out(multiplexer_7_out), .sel(in_2[6]));
  _16_Shift_Left u_16_shift_left_6 (.in(n16_shift_left_5_out), .out(n16_shift_left_6_out));
  _16_Shift_Left u_16_shift_left_7 (.in(n16_shift_left_6_out), .out(n16_shift_left_7_out));
  _16_adder u_16_adder_8 (.B(n16_adder_3_out), .A(n16_adder_11_out), .out(out_3));
  _16_adder u_16_adder_9 (.B(multiplexer_9_out), .A(multiplexer_10_out), .out(n16_adder_9_out));
  Multiplexer #(.width(16), .enable("false")) multiplexer_8 (
    .in0({16{1'b0}}), .in1(n16_shift_left_7_out), .out(multiplexer_8_out), .sel(in_2[7]));
  Multiplexer #(.width(16), .enable("false")) multiplexer_9 (
    .in0({16{1'b0}}), .in1(n16_shift_left_8_out), .out(multiplexer_9_out), .sel(in_2[8]));
  _16_Shift_Left u_16_shift_left_8 (.in(n16_shift_left_7_out), .out(n16_shift_left_8_out));
  _16_Shift_Left u_16_shift_left_9 (.in(n16_shift_left_8_out), .out(n16_shift_left_9_out));
  _16_adder u_16_adder_10 (.B(n16_adder_9_out), .A(n16_adder_12_out), .out(n16_adder_10_out));
  Multiplexer #(.width(16), .enable("false")) multiplexer_10 (
    .in0({16{1'b0}}), .in1(n16_shift_left_9_out), .out(multiplexer_10_out), .sel(in_2[9]));
  _16_Shift_Left u_16_shift_left_10 (.in(n16_shift_left_9_out), .out(n16_shift_left_10_out));
  _16_adder u_16_adder_11 (.B(n16_adder_10_out), .A(n16_adder_14_out), .out(n16_adder_11_out));
  _16_adder u_16_adder_12 (.B(multiplexer_12_out), .A(multiplexer_11_out), .out(n16_adder_12_out));
  Multiplexer #(.width(16), .enable("false")) multiplexer_11 (
    .in0({16{1'b0}}), .in1(n16_shift_left_12_out), .out(multiplexer_11_out), .sel(in_2[11]));
  Multiplexer #(.width(16), .enable("false")) multiplexer_12 (
    .in0({16{1'b0}}), .in1(n16_shift_left_10_out), .out(multiplexer_12_out), .sel(in_2[10]));
  _16_Shift_Left u_16_shift_left_11 (.in(n16_shift_left_12_out), .out(n16_shift_left_11_out));
  _16_Shift_Left u_16_shift_left_12 (.in(n16_shift_left_10_out), .out(n16_shift_left_12_out));
  _16_adder u_16_adder_13 (.B(multiplexer_13_out), .A(multiplexer_15_out), .out(n16_adder_13_out));
  Multiplexer #(.width(16), .enable("false")) multiplexer_13 (
    .in0({16{1'b0}}), .in1(n16_shift_left_11_out), .out(multiplexer_13_out), .sel(in_2[12]));
  _16_Shift_Left u_16_shift_left_13 (.in(n16_shift_left_11_out), .out(n16_shift_left_13_out));
  _16_adder u_16_adder_14 (.B(n16_adder_13_out), .A(n16_adder_15_out), .out(n16_adder_14_out));
  _16_adder u_16_adder_15 (.B(multiplexer_14_out), .A(multiplexer_16_out), .out(n16_adder_15_out));
  Multiplexer #(.width(16), .enable("false")) multiplexer_14 (
    .in0({16{1'b0}}), .in1(n16_shift_left_15_out), .out(multiplexer_14_out), .sel(in_2[14]));
  Multiplexer #(.width(16), .enable("false")) multiplexer_15 (
    .in0({16{1'b0}}), .in1(n16_shift_left_13_out), .out(multiplexer_15_out), .sel(in_2[13]));
  _16_Shift_Left u_16_shift_left_14 (.in(n16_shift_left_15_out), .out(n16_shift_left_14_out));
  _16_Shift_Left u_16_shift_left_15 (.in(n16_shift_left_13_out), .out(n16_shift_left_15_out));
  Multiplexer #(.width(16), .enable("false")) multiplexer_16 (
    .in0({16{1'b0}}), .in1(n16_shift_left_14_out), .out(multiplexer_16_out), .sel(in_2[15]));
endmodule

module Memory_Mapper (
  input  [15:0] RAM_Value_In,
  input  [15:0] RAM_Address_In,
  input  RAM_set,
  input  RAM_get,
  input  [15:0] Key_Value,
  input  Key_Enable,
  output RAM_set_2,
  output RAM_get_2,
  output [15:0] Ram_Value_Out,
  output [15:0] Ram_Address_Out,
  output [15:0] Screen_Value_Out,
  output [9:0] Screen_Address_Out,
  output Screen_Set
);

  wire clock_1_out, counter_1_q, screen_range_1_ram_value_out;
  wire [9:0] screen_adapter_1_out;

  Multiplexer #(.width(16), .disabled(0), .enable("false")) multiplexer_1 (
    .in0(RAM_Value_In), .in1(Key_Value), .out(Ram_Value_Out), .sel(counter_1_q));
  Multiplexer #(.width(16), .disabled(0), .enable("false")) multiplexer_2 (
    .in0(RAM_Address_In), .in1(16'hfafe), .out(Ram_Address_Out), .sel(counter_1_q));
  Clock clock_1 (.out(clock_1_out));
  Multiplexer #(.enable("false")) multiplexer_3 (.in0(RAM_set), .in1(Key_Enable), .out(RAM_set_2), .sel(counter_1_q));
  Counter #(.width(1), .max('h1)) counter_1 (
    .count(1'b1), .Q(counter_1_q), .clk(clock_1_out));  // open: load, D, carry, clr
  Screen_Adapter screen_adapter_1 (.in(RAM_Address_In), .out(screen_adapter_1_out));
  Screen_Range screen_range_1 (.Address(RAM_Address_In), .Ram_Value_Out(screen_range_1_ram_value_out));
  assign Screen_Value_Out = screen_range_1_ram_value_out ? RAM_Value_In : 16'bz;  // Controlled_Buffer controlled_buffer_1
  assign Screen_Address_Out = screen_range_1_ram_value_out ? screen_adapter_1_out : 10'bz;  // Controlled_Buffer controlled_buffer_2
  assign Screen_Set = screen_range_1_ram_value_out ? RAM_set : 1'bz;  // Controlled_Buffer controlled_buffer_3

  assign RAM_get_2 = RAM_get;

  // Notes on the sheet:
  //   NOTE: synchronize ram and screen cycle??
endmodule

module _10_to_16 (
  input  [9:0] in,
  output [15:0] out
);


  assign out = {{6{1'b0}}, in};
endmodule

module _8_to_16 (
  input  [7:0] in,
  output [15:0] out
);


  assign out = {{8{1'b0}}, in};
endmodule

module _16_to_10 (
  input  [15:0] in,
  output [9:0] out
);


  assign out = in[9:0];
endmodule

module Screen_Range (
  input  [15:0] Address,
  output Ram_Value_Out
);

  Comparator #(.width(16), .mode("unsigned")) comparator_1 (
    .a(Address), .b(16'hfbfe), .gt(Ram_Value_Out));  // open: eq, lt
endmodule

module Screen_Adapter (
  input  [15:0] in,
  output [9:0] out
);

  wire [15:0] subtractor_1_out;

  Subtractor #(.width(16)) subtractor_1 (.a(in), .b(16'hfc00), .out(subtractor_1_out));  // open: bin, bout
  _16_to_10 u_16_to_10_1 (.in(subtractor_1_out), .out(out));
endmodule

module _7_to_16 (
  input  [6:0] in,
  output [15:0] out
);


  assign out = {{9{1'b0}}, in};
endmodule
